# Fritzing sketch Platine (saved by Fritzing 0.9.10b)
circuit board: 8.46667cm x 5.64444cm
stripboards: 1

parts:
  Bauteil1 = Arduino Nano (Rev3.0)
  LCD1 = LCD screen
  R1 = Trimmer Potentiometer [maximum_resistance=10kΩ knob_status=50% power=0.5W package=THT]
  R2 = Resistor [tolerance=±5% power=0.25 resistance=560 package=THT]
  microSD1 = MicroSD Card Module
  RE1 = KY-040 Rotary encoder [package=THT]
  Reset = Pushbutton [package=THT]
  - = Pushbutton [package=THT]
  + = Pushbutton [package=THT]

nets:
  N1: Bauteil1.D1/TX, RE1.DT
  N2: Bauteil1.D0/RX, RE1.CLK
  GND: Bauteil1.GND, LCD1.VSS, LCD1.R/W, LCD1.LED-, R1.leg1, microSD1.GND, RE1.GND
  N3: Bauteil1.D2, RE1.SW
  N4: Bauteil1.D3, LCD1.RS
  N5: Bauteil1.D4, LCD1.E
  N6: Bauteil1.D5, LCD1.DB4
  N7: Bauteil1.D6, LCD1.DB5
  N8: Bauteil1.D7, LCD1.DB6
  N9: Bauteil1.D8, LCD1.DB7
  N10: Bauteil1.D9, R2.Pin_0
  N11: Bauteil1.D10, microSD1.CS
  N12: Bauteil1.D11/MOSI, microSD1.MOSI
  N13: Bauteil1.D12/MISO, microSD1.MISO
  VCC: Bauteil1.5V, LCD1.VDD, R1.leg2, microSD1.VCC, RE1.Vcc, Reset.leg1, -.leg1, +.leg1
  N14: Bauteil1.A2, +.leg0
  N15: Bauteil1.A1, -.leg0
  N16: Bauteil1.A0, Reset.leg0
  N17: Bauteil1.D13/SCK, microSD1.SCK
  N18: LCD1.V0, R1.wiper
  N19: LCD1.LED+, R2.Pin_1

custom parts:
  KY-040 Rotary encoder: KY-040 Rotary Encoder with switch on breakout borad from AZ Delivery
