# Fritzing sketch platine_breadboard_only (saved by Fritzing 0.9.10b)
circuit board: 8.46667cm x 5.64444cm
stripboards: 1

parts:
  Bauteil1 = Arduino Nano (Rev3.0) (ICSP)
  LCD1 = LCD screen
  R1 = Trimmer Potentiometer [maximum_resistance=10kΩ knob_status=50% power=0.5W package=THT]
  R2 = Resistor [tolerance=±5% power=0.25 resistance=560 package=THT]
  microSD1 = MicroSD Card Module
  S1 = Round Pushbutton
  S2 = Round Pushbutton
  S3 = Round Pushbutton
  R4 = Resistor [tolerance=±5% power=0.25 resistance=10k package=THT]
  R5 = Resistor [tolerance=±5% power=0.25 resistance=10k package=THT]
  R6 = Resistor [tolerance=±5% power=0.25 resistance=10k package=THT]
  J1 = Power Jack [package=power_jack_combo]
  RE1 = KY-040 Rotary encoder [package=THT]
  D1 = Rectifier Diode [part_number=1N4001 package="300 mil [THT]"]

nets:
  N1: Bauteil1.D1/TX, RE1.CLK, D1.cathode
  N2: Bauteil1.D0/RX, RE1.DT
  GND: Bauteil1.GND, LCD1.VSS, LCD1.R/W, LCD1.LED-, R1.leg2, microSD1.GND, R4.Pin_1, R5.Pin_1, R6.Pin_1, J1.GNDBREAK, RE1.GND
  N3: Bauteil1.D2, RE1.SW, D1.anode
  N4: Bauteil1.D3, LCD1.RS
  N5: Bauteil1.D4, LCD1.E
  N6: Bauteil1.D5, LCD1.DB4
  N7: Bauteil1.D6, LCD1.DB5
  N8: Bauteil1.D7, LCD1.DB6
  N9: Bauteil1.D8, LCD1.DB7
  N10: Bauteil1.D9, R2.Pin_1
  N11: Bauteil1.D10, microSD1.CS
  N12: Bauteil1.D11/MOSI, microSD1.MOSI
  N13: Bauteil1.D12/MISO, microSD1.VCC, microSD1.MISO
  N14: Bauteil1.VIN, J1.PWR
  N15: Bauteil1.5V, S1.leg0, S2.leg0, S3.leg0
  N16: Bauteil1.A6, S1.leg1, R4.Pin_0
  N17: Bauteil1.A5, S3.leg1, R5.Pin_0
  N18: Bauteil1.A4, S2.leg1, R6.Pin_0
  N19: Bauteil1.D13/SCK, microSD1.SCK
  VDD: LCD1.VDD, R1.leg1, RE1.Vcc
  N20: LCD1.V0, R1.wiper
  N21: LCD1.LED+, R2.Pin_0

custom parts:
  KY-040 Rotary encoder: KY-040 Rotary Encoder with switch on breakout borad from AZ Delivery
